// Logisim project all.circ as structural Verilog: 14 circuits, main circuit main
module main (
  input  x,
  input  y,
  input  Cin,
  output Sum,
  output Cout
);

  wire and_1_out, and_3_out, and_4_out, not_1_out, not_2_out, not_3_out, not_4_out, not_5_out, not_6_out,
       or_1_out, or_2_out, or_3_out, or_4_out, or_5_out, or_6_out, or_7_out, or_8_out, or_9_out, or_10_out,
       or_11_out;

  not not_1 (not_1_out, y);
  not not_2 (not_2_out, x);
  not not_3 (not_3_out, x);
  not not_4 (not_4_out, y);
  or or_1 (or_1_out, x, y);
  or or_2 (or_2_out, x, Cin);
  or or_3 (or_3_out, x, y);
  or or_4 (or_4_out, x, not_1_out);
  not not_5 (not_5_out, Cin);
  or or_5 (or_5_out, not_2_out, y);
  not not_6 (not_6_out, Cin);
  or or_6 (or_6_out, not_3_out, not_4_out);
  and and_1 (and_1_out, or_1_out, or_2_out);
  or or_7 (or_7_out, y, Cin);
  or or_8 (or_8_out, or_3_out, Cin);
  or or_9 (or_9_out, or_4_out, not_5_out);
  or or_10 (or_10_out, or_5_out, not_6_out);
  or or_11 (or_11_out, or_6_out, Cin);
  and and_2 (Cout, and_1_out, or_7_out);
  and and_3 (and_3_out, or_8_out, or_9_out);
  and and_4 (and_4_out, or_10_out, or_11_out);
  and and_5 (Sum, and_3_out, and_4_out);
endmodule

module test (
  input  x,
  input  y,
  output z
);

  wire and_1_out, or_1_out;

  and and_1 (and_1_out, x, y);
  or or_1 (or_1_out, x, y);
  and and_2 (z, and_1_out, or_1_out);
endmodule

module toy (
  input  x,
  input  y,
  output z
);

  and and_1 (z, x, y);
endmodule

module wiring_tut (
  input  [7:0] in_1,
  input  [2:0] in_2,
  input  [7:0] in_3,
  input  [7:0] in_4,
  input  [7:0] in_5,
  input  in_6,
  output [3:0] out_7,
  output [2:0] out_8,
  output [2:0] out_9,
  output out_10,
  output [3:0] out_11,
  output [15:0] out_12,
  output [15:0] out_13
);

  Pull_Resistor #(.pull(1)) pull_resistor_1 (.node(in_2));
  Clock clock_1 (.out(out_10));
  Bit_Extender #(.out_width(4)) bit_extender_1 (.in(in_3), .out(out_11));
  assign out_12 = {{8{in_4[7]}}, in_4};  // Bit_Extender bit_extender_2
  assign out_13 = {{8{in_6}}, in_5};  // Bit_Extender bit_extender_3
  // Probe on {in_1[4], in_1[2:0]}

  assign out_7 = {in_1[4], in_1[2:0]};
  assign out_8 = in_2;
  assign out_9 = in_2;

  // Other names for the same wires on the sheet: ld[2:0] = in_2
endmodule

module gates_tut (
  input  in_1,
  input  in_2,
  input  in_3,
  input  in_4,
  input  in_5,
  input  in_6,
  input  in_7,
  input  in_8,
  input  in_9,
  output out_10,
  output out_11,
  output out_12,
  output out_13
);

  assign out_13 = in_9 ? in_8 : 1'bz;  // Controlled_Buffer controlled_buffer_1
  xor xor_1 (out_10, in_1, in_2, in_3);
  xor odd_parity_1 (out_11, in_4, in_5);
  xnor even_parity_1 (out_12, in_6, in_7);
endmodule

module plexers (
  input  [3:0] in_1,
  input  [3:0] in_2,
  input  [3:0] in_3,
  input  [3:0] in_4,
  input  [1:0] in_5,
  input  in_6,
  input  [3:0] in_7,
  input  [1:0] in_8,
  input  [1:0] in_9,
  input  in_10,
  input  in_11,
  input  in_12,
  input  in_13,
  input  in_14,
  input  in_15,
  output [3:0] out_16,
  output [3:0] out_17,
  output [3:0] out_18,
  output [3:0] out_19,
  output [3:0] out_20,
  output out_21,
  output out_22,
  output out_23,
  output out_24,
  output [2:0] out_25,
  output out_26
);

  Demultiplexer #(.select(2), .width(4), .enable("false")) demultiplexer_1 (
    .out0(out_17), .out1(out_18), .out2(out_19), .out3(out_20), .in(in_7), .sel(in_8));
  Decoder #(.select(2), .enable("false")) decoder_1 (
    .out0(out_21), .out1(out_22), .out2(out_23), .out3(out_24), .sel(in_9));
  Priority_Encoder priority_encoder_1 (
    .in0(in_11), .in2(in_12), .in4(in_13), .in6(in_14), .out(out_25), .en_in(in_15), .gs(out_26),
    .en_out(in_10));  // open: in1, in3, in5, in7
  Multiplexer #(.select(2), .width(4), .enable("false")) multiplexer_1 (
    .in0(in_1), .in1(in_2), .in2(in_3), .in3(in_4), .out(out_16), .sel(in_5));
endmodule

module arith_tut (
  input  in_1,
  input  in_2,
  input  [3:0] in_3,
  input  [3:0] in_4,
  input  [3:0] in_5,
  input  [3:0] in_6,
  input  in_7,
  input  in_8,
  input  [3:0] in_9,
  input  [3:0] in_10,
  input  [3:0] in_11,
  input  [3:0] in_12,
  input  [3:0] in_13,
  input  [3:0] in_14,
  input  [3:0] in_15,
  input  [7:0] in_16,
  input  [7:0] in_17,
  input  [7:0] in_18,
  input  [2:0] in_19,
  output [3:0] out_20,
  output [3:0] out_21,
  output out_22,
  output out_23,
  output [3:0] out_24,
  output [3:0] out_25,
  output out_26,
  output out_27,
  output [3:0] out_28,
  output [7:0] out_29,
  output [3:0] out_30,
  output out_31,
  output out_32,
  output out_33,
  output [7:0] out_34
);

  // Probe on in_14
  // Probe on in_15
  // Probe on in_3
  // Probe on in_5
  // Probe on in_10
  // Probe on in_12
  Multiplier #(.width(4)) multiplier_1 (.a(in_14), .b(in_15), .out(out_28), .cin(in_13), .cout(out_29[7:4]));
  // Probe on out_20
  Adder #(.width(4)) adder_1 (.a(in_3), .b(in_5), .out(out_20), .cin(in_1), .cout(out_22));
  // Probe on out_25
  Adder #(.width(4)) adder_2 (.a(in_10), .b(in_12), .out(out_25), .cin(in_7), .cout(out_27));
  // Probe on {out_29[7:4], out_28}
  Comparator comparator_1 (.a(in_16), .b(in_17), .gt(out_31), .eq(out_32), .lt(out_33));
  Shifter #(.shift("rl")) shifter_1 (.in(in_18), .\dist (in_19), .out(out_34));
  // Probe on in_4
  // Probe on in_6
  // Probe on in_9
  // Probe on in_11
  Subtractor #(.width(4)) subtractor_1 (.a(in_4), .b(in_6), .out(out_21), .bin(in_2), .bout(out_23));
  Subtractor #(.width(4)) subtractor_2 (.a(in_9), .b(in_11), .out(out_24), .bin(in_8), .bout(out_26));
  // Probe on out_21
  // Probe on out_24

  assign out_29[3:0] = out_28;
  assign out_30 = out_29[7:4];
endmodule

module mem (
  input  [7:0] in_1,
  input  in_2,
  input  in_3,
  input  [7:0] in_4,
  input  in_5,
  input  in_6,
  input  in_7,
  input  in_8,
  input  in_9,
  input  in_10,
  input  [7:0] in_11,
  input  [7:0] in_12,
  input  in_13,
  input  [7:0] in_14,
  input  [7:0] in_15,
  input  [7:0] in_16,
  input  in_17,
  input  in_18,
  output [7:0] out_19,
  output out_20,
  output out_21,
  output [7:0] out_22,
  output out_23,
  output [7:0] out_24,
  output [7:0] out_25,
  output [7:0] out_26
);

  wire clock_1_out, clock_2_out, clock_3_out, clock_4_out, clock_5_out, clock_6_out, not_1_out;
  wire [7:0] controlled_buffer_1_out;
  wire [31:0] multiplexer_1_out;
  wire [31:8] register_1_q;

  Multiplexer #(.width(8)) multiplexer_1 (
    .in0(in_1), .in1({8{1'b0}}), .out(multiplexer_1_out[7:0]), .sel(in_2));  // open: en
  Shift_Register #(.width(8)) shift_register_1 (
    .shift(in_10), .in(in_11), .clk(clock_1_out), .out(out_24));  // open: load, clr, d0, q0, d1, q1, d2, q2, d3, q3, d4, q4, d5, q5, d6, q6, d7, q7
  Clock clock_1 (.out(clock_1_out));
  Register #(.width(32)) register_1 (
    .D(multiplexer_1_out), .Q({register_1_q, out_19}), .clk(clock_2_out));  // open: en, clr
  Clock clock_2 (.out(clock_2_out));
  Counter counter_1 (.load(in_3), .D(in_4), .count(in_7), .Q(out_22), .clk(clock_3_out), .clr(in_8));  // open: carry
  // Probe on out_22
  Clock clock_3 (.out(clock_3_out));
  Clock clock_4 (.out(clock_4_out));
  ROM rom_1 (.addr(out_22), .data(out_25));  // open: sel
  RAM #(.bus("separate")) ram_1 (
    .addr(in_15), .din(in_16), .data(out_26), .str(in_17), .clk(clock_4_out), .ld(in_18));  // open: sel, clr
  Clock clock_5 (.out(clock_5_out));
  D_Flip_Flop d_ff_1 (.clk(clock_5_out), .D(in_9), .Q(out_23), .preset(in_6), .reset(in_5));  // open: Qn, en
  T_Flip_Flop t_ff_1 (.clk(clock_5_out), .preset(in_6), .reset(in_5));  // open: T, Q, Qn, en
  assign controlled_buffer_1_out = in_13 ? in_12 : 8'bz;  // Controlled_Buffer controlled_buffer_1
  J_K_Flip_Flop j_k_ff_1 (.clk(clock_5_out), .preset(in_6), .reset(in_5));  // open: J, K, Q, Qn, en
  not not_1 (not_1_out, in_13);
  Clock clock_6 (.out(clock_6_out));
  S_R_Flip_Flop s_r_ff_1 (.clk(clock_5_out), .Q(out_20), .Qn(out_21), .preset(in_6), .reset(in_5));  // open: S, R, en
  RAM ram_2 (.addr(in_14), .data(controlled_buffer_1_out), .clk(clock_6_out), .ld(not_1_out));  // open: sel, clr
  // Pins of 8 and 32 bits meet at {register_1_q, out_19}
  // Pins of 8 and 32 bits meet at multiplexer_1_out

  // Notes on the sheet:
  //   contents of rom_1 (hex, n*v repeats v):
  //   23 67 ab e0 14*0 11
endmodule

module io_tut (
  input  clr,
  input  rd_enable,
  input  wenable,
  input  clr_2,
  input  [3:0] in_5,
  input  in_6,
  output has
);

  wire clock_1_out;
  wire [6:0] keyboard_1_data;

  Keyboard keyboard_1 (.clk(clock_1_out), .re(rd_enable), .clr(clr), .avail(has), .data(keyboard_1_data));
  Hex_Digit_Display hex_digit_display_1 (.value(in_5), .dp(in_6));
  TTY tty_1 (.data(keyboard_1_data), .clk(clock_1_out), .we(wenable), .clr(clr_2));
  Clock clock_1 (.out(clock_1_out));
endmodule

module try1 (
  input  [7:0] In8,
  input  Reset,
  output [7:0] Out8
);

  wire clock_1_out;
  wire [7:0] multiplexer_1_out;

  Multiplexer #(.width(8)) multiplexer_1 (
    .in0(In8), .in1({8{1'b0}}), .out(multiplexer_1_out), .sel(Reset));  // open: en
  Register register_1 (.D(multiplexer_1_out), .Q(Out8), .clk(clock_1_out));  // open: en, clr
  Clock clock_1 (.out(clock_1_out));
endmodule

module import_tut (
  input  [7:0] in_1,
  input  in_2,
  output [7:0] out_3
);

  Clock clock_1 ();  // open: out
  try1 try1_1 (.In8(in_1), .Out8(out_3), .Reset(in_2));
endmodule

module led_1 (
  input  In1,
  input  In2,
  input  In3,
  input  In4,
  input  In5,
  output Out1,
  output Out2,
  output Out3,
  output Out4,
  output Out5
);

  or or_1 (Out1, In1, In2, In3, In4, In5);
  or or_2 (Out2, In2, In3, In4, In5);
  or or_3 (Out3, In3, In4, In5);
  or or_4 (Out4, In4, In5);

  assign Out5 = In5;
endmodule

module led_encoder (
  input  In1,
  input  In2,
  input  In3,
  input  In4,
  input  In5,
  output Out1,
  output Out2,
  output Out3
);

  wire and_1_out, and_2_out, and_3_out, and_4_out, not_1_out, not_2_out, not_3_out, not_4_out, not_5_out,
       not_6_out, not_7_out;

  not not_1 (not_1_out, In4);
  not not_2 (not_2_out, In2);
  not not_3 (not_3_out, In4);
  not not_4 (not_4_out, In4);
  not not_5 (not_5_out, In5);
  not not_6 (not_6_out, In4);
  not not_7 (not_7_out, In5);
  or or_1 (Out3, In5, In4);
  and and_1 (and_1_out, In3, not_1_out);
  and and_2 (and_2_out, In1, not_2_out, not_3_out);
  and and_3 (and_3_out, In3, not_4_out, not_5_out);
  and and_4 (and_4_out, In2, not_6_out, not_7_out);
  or or_2 (Out1, In5, and_1_out, and_2_out);
  or or_3 (Out2, and_3_out, and_4_out);
endmodule

module led_whole (
);

  wire _1_out, _2_out, _3_out, _4_out, _5_out, led_1_1_out1, led_1_1_out2, led_1_1_out3, led_1_1_out4,
       led_1_1_out5;
  wire [2:0] led_encoder_1_out1;

  Button _1 (.out(_1_out));
  Button _2 (.out(_2_out));
  Button _3 (.out(_3_out));
  Button _4 (.out(_4_out));
  Button _5 (.out(_5_out));
  led_1 led_1_1 (
    .In1(_1_out), .In2(_2_out), .In3(_3_out), .In4(_4_out), .In5(_5_out), .Out1(led_1_1_out1),
    .Out2(led_1_1_out2), .Out3(led_1_1_out3), .Out4(led_1_1_out4), .Out5(led_1_1_out5));
  led_encoder led_encoder_1 (
    .In1(_1_out), .In2(_2_out), .In3(_3_out), .In4(_4_out), .In5(_5_out), .Out1(led_encoder_1_out1[0]),
    .Out2(led_encoder_1_out1[1]), .Out3(led_encoder_1_out1[2]));
  LED led_1 (.in(led_1_1_out1));
  LED led_2 (.in(led_1_1_out2));
  LED led_3 (.in(led_1_1_out3));
  LED led_4 (.in(led_1_1_out4));
  LED led_5 (.in(led_1_1_out5));
  Hex_Digit_Display hex_digit_display_1 (.value({1'b0, led_encoder_1_out1}), .dp(1'b1));
endmodule
