// Logisim project single_cycle_mips_cpu.circ as structural Verilog: 15 circuits, main circuit MIPS_C7
module MIPS_C7 (
  input  in_1
);

  wire alu_1_equal, ALUSrc, CLK, ExtOp, IfBrch, MemToReg, MemWrite, nPC_sel, RegDst, RegWrite, ShiftSel;
  wire [2:0] ALUCtl;
  wire [4:0] instrsplitter_1__15_11, instrsplitter_1__20_16, instrsplitter_1__25_21, multiplexer_1_out;
  wire [5:0] instrsplitter_1_func, instrsplitter_1_opcode;
  wire [15:0] instrsplitter_1_imm;
  wire [31:0] alu_1_aluout, dm_1_rddata, ext_1_dout, grf_1_rd1, grf_1_rd2, ifu_1_instr, multiplexer_2_out,
       multiplexer_3_out, multiplexer_4_out, multiplexer_5_out, shifter_1_out;

  Clock clock_1 (.out(CLK));
  IFU ifu_1 (.Instr(ifu_1_instr), .CLK(CLK), .Reset(in_1), .WrdOffset(ext_1_dout), .IfBrch(IfBrch));
  // Probe on ifu_1_instr
  InstrSplitter instrsplitter_1 (
    .Instru(ifu_1_instr), .OpCode(instrsplitter_1_opcode), .func(instrsplitter_1_func),
    ._25_21(instrsplitter_1__25_21), ._20_16(instrsplitter_1__20_16), ._15_11(instrsplitter_1__15_11),
    .Imm(instrsplitter_1_imm));
  // Probe on instrsplitter_1__25_21
  // Probe on instrsplitter_1__20_16
  // Probe on instrsplitter_1__15_11
  Controller controller_1 (
    .func(instrsplitter_1_func), .op(instrsplitter_1_opcode), .RegDst(RegDst), .ALUSrc(ALUSrc),
    .MemToReg(MemToReg), .RegWrite(RegWrite), .MemWrite(MemWrite), .nPC_sel(nPC_sel), .ExtOp(ExtOp),
    .ALUCtl(ALUCtl), .ShiftSel(ShiftSel));
  Multiplexer #(.width(5), .enable("false")) multiplexer_1 (
    .in0(instrsplitter_1__20_16), .in1(instrsplitter_1__15_11), .out(multiplexer_1_out), .sel(RegDst));
  EXT ext_1 (.Din(instrsplitter_1_imm), .Dout(ext_1_dout), .ExtSign(ExtOp));
  // Probe on ext_1_dout
  Shifter #(.width(32)) shifter_1 (.in(ext_1_dout), .\dist (5'b10000), .out(shifter_1_out));
  // Probe on shifter_1_out
  // Probe on multiplexer_2_out
  GRF grf_1 (
    .RD1_num(instrsplitter_1__25_21), .RD2_num(instrsplitter_1__20_16), .in_6(in_1),
    .W_num(multiplexer_1_out), .WD(multiplexer_2_out), .RD1(grf_1_rd1), .RD2(grf_1_rd2), .WE(RegWrite),
    .in_5(CLK));
  Multiplexer #(.width(32), .enable("false")) multiplexer_2 (
    .in0(multiplexer_5_out), .in1(multiplexer_3_out), .out(multiplexer_2_out), .sel(ShiftSel));
  Multiplexer #(.width(32), .enable("false")) multiplexer_3 (
    .in0(ext_1_dout), .in1(shifter_1_out), .out(multiplexer_3_out), .sel(ShiftSel));
  // Probe on grf_1_rd1
  // Probe on multiplexer_3_out
  // Probe on grf_1_rd2
  ALU alu_1 (
    .ALUCtl(ALUCtl), .ALUOut(alu_1_aluout), .Equal(alu_1_equal), .operand1(grf_1_rd1),
    .operand2(multiplexer_4_out));
  Multiplexer #(.width(32), .enable("false")) multiplexer_4 (
    .in0(grf_1_rd2), .in1(multiplexer_3_out), .out(multiplexer_4_out), .sel(ALUSrc));
  // Probe on ALUCtl
  Multiplexer #(.width(32), .enable("false")) multiplexer_5 (
    .in0(alu_1_aluout), .in1(dm_1_rddata), .out(multiplexer_5_out), .sel(MemToReg));
  // Probe on multiplexer_4_out
  // Probe on alu_1_aluout
  and and_1 (IfBrch, nPC_sel, alu_1_equal);
  DM dm_1 (
    .MemAddr(alu_1_aluout), .MemData(grf_1_rd2), .MemWrite(MemWrite), .RdData(dm_1_rddata), .CLK(CLK),
    .Reset(in_1));

  // Other names for the same wires on the sheet: Reset = in_1

  // Notes on the sheet:
  //   in_1: pull=down
endmodule

module IFU (
  input  [31:0] WrdOffset,
  input  IfBrch,
  input  CLK,
  input  Reset,
  output [31:0] Instr
);

  wire [29:0] adder_1_out, adder_2_out, multiplexer_1_out, multiplexer_2_out, PC_q;

  Adder #(.width(30)) adder_1 (.a(WrdOffset[29:0]), .b(adder_2_out), .out(adder_1_out));  // open: cin, cout
  Multiplexer #(.width(30), .disabled(0), .enable("false")) multiplexer_1 (
    .in0(adder_2_out), .in1(adder_1_out), .out(multiplexer_1_out), .sel(IfBrch));
  Multiplexer #(.width(30), .disabled(0), .enable("false")) multiplexer_2 (
    .in0(multiplexer_1_out), .in1(30'h3000), .out(multiplexer_2_out), .sel(Reset));
  Clock clock_1 ();  // open: out
  // Probe on PC_q
  Register #(.width(30)) PC (.D(multiplexer_2_out), .Q(PC_q), .clk(CLK));  // open: en, clr
  // Probe on PC_q[4:0]
  Adder #(.width(30)) adder_2 (.a(PC_q), .b(30'h1), .out(adder_2_out));  // open: cin, cout
  // Probe on Instr
  ROM #(.addrWidth(5), .dataWidth(32)) rom_1 (.addr(PC_q[4:0]), .data(Instr));  // open: sel

  // Notes on the sheet:
  //   WrdOffset: pull=down
  //   IfBrch: pull=down
  //   Instr: pull=down
  //   CLK: pull=down
  //   Reset: pull=down
  //   contents of rom_1 (hex, n*v repeats v):
  //   341f0001 34080000 34100004 341e0003 1104021 3c0c1234 358d0087 36530065 272a023 291a821 36b60043
  //   ac160008 ac150004 8c170004 8c180008 1200000e 2f8c821 34040010 34050018 ac99fffc acbafff8 8c86fff8
  //   8ca7fff4 34a20999 ac820004 21f8023 121effe9 3dff023 121e0001 8c890004 8c8a0004
endmodule

module ALU (
  input  [31:0] operand1,
  input  [31:0] operand2,
  input  [2:0] ALUCtl,
  output [31:0] ALUOut,
  output Equal
);

  wire [31:0] adder_1_out, or_1_out, subtractor_1_out;

  Adder #(.width(32)) adder_1 (.a(operand1), .b(operand2), .out(adder_1_out));  // open: cin, cout
  Subtractor #(.width(32)) subtractor_1 (.a(operand1), .b(operand2), .out(subtractor_1_out));  // open: bin, bout
  assign or_1_out = operand1 | operand2;  // OR_Gate or_1, 32 bits wide
  Comparator #(.width(32), .mode("unsigned")) comparator_1 (.a(operand1), .b(operand2), .eq(Equal));  // open: gt, lt
  Multiplexer #(.select(3), .width(32), .disabled(0), .enable("false")) multiplexer_1 (
    .in1(or_1_out), .in2(subtractor_1_out), .in4(adder_1_out), .out(ALUOut), .sel(ALUCtl));  // open: in0, in3, in5, in6, in7
  // Probe on operand1
  // Probe on operand2
  // Probe on ALUOut

  // Other names for the same wires on the sheet: op1[31:0] = operand1; op2[31:0] = operand2

  // Notes on the sheet:
  //   Equal: pull=down
  //   100  Add->4
  //   010  Sub->2
  //   001  OR->1
endmodule

module GRF (
  input  [4:0] RD1_num,
  input  [4:0] RD2_num,
  input  [4:0] W_num,
  input  [31:0] WD,
  input  in_5,
  input  in_6,
  input  WE,
  output [31:0] RD1,
  output [31:0] RD2
);

  wire WE1, WE2, WE3, WE4, WE5, WE6, WE7, WE8, WE9, WE10, WE11, WE12, WE13, WE14, WE15, WE16, WE17, WE18,
       WE19, WE20, WE21, WE22, WE23, WE24, WE25, WE26, WE27, WE28, WE29, WE30, WE31;
  wire [31:0] D1, D2, D3, D4, D5, D6, D7, D8, D9, D10, D11, D12, D13, D14, D15, D16, D17, D18, D19, D20, D21,
       D22, D23, D24, D25, D26, D27, D28, D29, D30, D31;

  Register #(.width(32)) R1 (.D(WD), .en(WE1), .Q(D1), .clk(in_5), .clr(in_6));
  Register #(.width(32)) R2 (.D(WD), .en(WE2), .Q(D2), .clk(in_5), .clr(in_6));
  Register #(.width(32)) R3 (.D(WD), .en(WE3), .Q(D3), .clk(in_5), .clr(in_6));
  Register #(.width(32)) R4 (.D(WD), .en(WE4), .Q(D4), .clk(in_5), .clr(in_6));
  Register #(.width(32)) R5 (.D(WD), .en(WE5), .Q(D5), .clk(in_5), .clr(in_6));
  Register #(.width(32)) R6 (.D(WD), .en(WE6), .Q(D6), .clk(in_5), .clr(in_6));
  Register #(.width(32)) R7 (.D(WD), .en(WE7), .Q(D7), .clk(in_5), .clr(in_6));
  // Probe on RD1
  Register #(.width(32)) R8 (.D(WD), .en(WE8), .Q(D8), .clk(in_5), .clr(in_6));
  Register #(.width(32)) R9 (.D(WD), .en(WE9), .Q(D9), .clk(in_5), .clr(in_6));
  Register #(.width(32)) R10 (.D(WD), .en(WE10), .Q(D10), .clk(in_5), .clr(in_6));
  Register #(.width(32)) R11 (.D(WD), .en(WE11), .Q(D11), .clk(in_5), .clr(in_6));
  Register #(.width(32)) R12 (.D(WD), .en(WE12), .Q(D12), .clk(in_5), .clr(in_6));
  Register #(.width(32)) R13 (.D(WD), .en(WE13), .Q(D13), .clk(in_5), .clr(in_6));
  Register #(.width(32)) R14 (.D(WD), .en(WE14), .Q(D14), .clk(in_5), .clr(in_6));
  Register #(.width(32)) R15 (.D(WD), .en(WE15), .Q(D15), .clk(in_5), .clr(in_6));
  // Probe on RD2
  Register #(.width(32)) R16 (.D(WD), .en(WE16), .Q(D16), .clk(in_5), .clr(in_6));
  Register #(.width(32)) R17 (.D(WD), .en(WE17), .Q(D17), .clk(in_5), .clr(in_6));
  Register #(.width(32)) R18 (.D(WD), .en(WE18), .Q(D18), .clk(in_5), .clr(in_6));
  Register #(.width(32)) R19 (.D(WD), .en(WE19), .Q(D19), .clk(in_5), .clr(in_6));
  Register #(.width(32)) R20 (.D(WD), .en(WE20), .Q(D20), .clk(in_5), .clr(in_6));
  Register #(.width(32)) R21 (.D(WD), .en(WE21), .Q(D21), .clk(in_5), .clr(in_6));
  Register #(.width(32)) R22 (.D(WD), .en(WE22), .Q(D22), .clk(in_5), .clr(in_6));
  Register #(.width(32)) R23 (.D(WD), .en(WE23), .Q(D23), .clk(in_5), .clr(in_6));
  Register #(.width(32)) R24 (.D(WD), .en(WE24), .Q(D24), .clk(in_5), .clr(in_6));
  Register #(.width(32)) R25 (.D(WD), .en(WE25), .Q(D25), .clk(in_5), .clr(in_6));
  Register #(.width(32)) R26 (.D(WD), .en(WE26), .Q(D26), .clk(in_5), .clr(in_6));
  Register #(.width(32)) R27 (.D(WD), .en(WE27), .Q(D27), .clk(in_5), .clr(in_6));
  Register #(.width(32)) R28 (.D(WD), .en(WE28), .Q(D28), .clk(in_5), .clr(in_6));
  Register #(.width(32)) R29 (.D(WD), .en(WE29), .Q(D29), .clk(in_5), .clr(in_6));
  Register #(.width(32)) R30 (.D(WD), .en(WE30), .Q(D30), .clk(in_5), .clr(in_6));
  Register #(.width(32)) R31 (.D(WD), .en(WE31), .Q(D31), .clk(in_5), .clr(in_6));
  Decoder #(.select(5), .disabled(0)) decoder_1 (
    .out1(WE1), .out2(WE2), .out3(WE3), .out4(WE4), .out5(WE5), .out6(WE6), .out7(WE7), .out8(WE8),
    .out9(WE9), .out10(WE10), .out11(WE11), .out12(WE12), .out13(WE13), .out14(WE14), .out15(WE15),
    .out16(WE16), .out17(WE17), .out18(WE18), .out19(WE19), .out20(WE20), .out21(WE21), .out22(WE22),
    .out23(WE23), .out24(WE24), .out25(WE25), .out26(WE26), .out27(WE27), .out28(WE28), .out29(WE29),
    .out30(WE30), .out31(WE31), .sel(W_num), .en(WE));  // open: out0
  Multiplexer #(.select(5), .width(32), .enable("false")) multiplexer_1 (
    .in0({32{1'b0}}), .in1(D1), .in2(D2), .in3(D3), .in4(D4), .in5(D5), .in6(D6), .in7(D7), .in8(D8),
    .in9(D9), .in10(D10), .in11(D11), .in12(D12), .in13(D13), .in14(D14), .in15(D15), .in16(D16), .in17(D17),
    .in18(D18), .in19(D19), .in20(D20), .in21(D21), .in22(D22), .in23(D23), .in24(D24), .in25(D25),
    .in26(D26), .in27(D27), .in28(D28), .in29(D29), .in30(D30), .in31(D31), .out(RD1), .sel(RD1_num));
  Multiplexer #(.select(5), .width(32), .enable("false")) multiplexer_2 (
    .in0({32{1'b0}}), .in1(D1), .in2(D2), .in3(D3), .in4(D4), .in5(D5), .in6(D6), .in7(D7), .in8(D8),
    .in9(D9), .in10(D10), .in11(D11), .in12(D12), .in13(D13), .in14(D14), .in15(D15), .in16(D16), .in17(D17),
    .in18(D18), .in19(D19), .in20(D20), .in21(D21), .in22(D22), .in23(D23), .in24(D24), .in25(D25),
    .in26(D26), .in27(D27), .in28(D28), .in29(D29), .in30(D30), .in31(D31), .out(RD2), .sel(RD2_num));

  // Other names for the same wires on the sheet: CLK = in_5; Out1[31:0] = RD1; Out2[31:0] = RD2; Reset = in_6;
  //   sel1[4:0] = RD1_num; sel2[4:0] = RD2_num; wsel[4:0] = W_num

  // Notes on the sheet:
  //   WE: pull=down
  //   RD1: pull=down
  //   in_5: pull=down
  //   RD2: pull=down
  //   in_6: pull=down
endmodule

module DM (
  input  [31:0] MemAddr,
  input  [31:0] MemData,
  input  MemWrite,
  input  CLK,
  input  Reset,
  output [31:0] RdData
);

  wire buffer_1_out, not_1_out;

  buf buffer_1 (buffer_1_out, MemWrite);
  Clock clock_1 ();  // open: out
  not not_1 (not_1_out, MemWrite);
  RAM #(.addrWidth(5), .dataWidth(32), .bus("separate")) ram_1 (
    .addr(MemAddr[6:2]), .din(MemData), .data(RdData), .str(buffer_1_out), .clk(CLK), .ld(not_1_out),
    .clr(Reset));  // open: sel

  // Notes on the sheet:
  //   CLK: pull=down
  //   Reset: pull=down
  //   RdData: pull=down
  //   MemWrite: pull=down
endmodule

module Op_func_TO_Instr (
  input  op31,
  input  op30,
  input  op29,
  input  op28,
  input  op27,
  input  op26,
  input  fun5,
  input  fun4,
  input  fun3,
  input  fun2,
  input  fun1,
  input  fun0,
  output addu,
  output subu,
  output ori,
  output lui,
  output lw,
  output sw,
  output beq
);

  wire beq_out, buffer_1_out, buffer_2_out, buffer_3_out, buffer_4_out, buffer_5_out, buffer_6_out, lui_out,
       lw_out, not_1_out, not_2_out, not_3_out, not_4_out, not_5_out, not_6_out, not_7_out, ori_out,
       RType_out, sw_out;

  buf buffer_1 (buffer_1_out, op31);
  not not_1 (not_1_out, op31);
  not not_2 (not_2_out, op30);
  buf buffer_2 (buffer_2_out, op29);
  buf buffer_3 (buffer_3_out, op28);
  not not_3 (not_3_out, op29);
  buf buffer_4 (buffer_4_out, op27);
  not not_4 (not_4_out, op28);
  not not_5 (not_5_out, op27);
  buf buffer_5 (buffer_5_out, op26);
  not not_6 (not_6_out, op26);
  and RType (RType_out, not_1_out, not_2_out, not_3_out, not_4_out, not_5_out, not_6_out);
  and u_ori (ori_out, not_1_out, not_2_out, buffer_2_out, buffer_3_out, not_5_out, buffer_5_out);
  and u_lui (lui_out, not_1_out, not_2_out, buffer_2_out, buffer_3_out, buffer_4_out, buffer_5_out);
  and u_lw (lw_out, buffer_1_out, not_2_out, not_3_out, not_4_out, buffer_4_out, buffer_5_out);
  and u_sw (sw_out, buffer_1_out, not_2_out, buffer_2_out, not_4_out, buffer_4_out, buffer_5_out);
  and u_beq (beq_out, not_1_out, not_2_out, not_3_out, buffer_3_out, not_5_out, not_6_out);
  buf buffer_6 (buffer_6_out, fun1);
  not not_7 (not_7_out, fun1);
  buf buffer_7 (ori, ori_out);
  buf buffer_8 (lui, lui_out);
  buf buffer_9 (lw, lw_out);
  buf buffer_10 (sw, sw_out);
  buf buffer_11 (beq, beq_out);
  and u_addu (addu, RType_out, not_7_out);
  and u_subu (subu, RType_out, buffer_6_out);

  // Notes on the sheet:
  //   sw: pull=down
  //   ori: pull=down
  //   beq: pull=down
  //   addu: pull=down
  //   lw: pull=down
  //   lui: pull=down
  //   subu: pull=down
endmodule

module EXT (
  input  [15:0] Din,
  input  ExtSign,
  output [31:0] Dout
);

  wire [31:0] bit_extender_1_out, bit_extender_2_out;

  assign bit_extender_1_out = {{16{1'b0}}, Din};  // Bit_Extender bit_extender_1
  assign bit_extender_2_out = {{16{Din[15]}}, Din};  // Bit_Extender bit_extender_2
  Multiplexer #(.width(32), .enable("false")) multiplexer_1 (
    .in0(bit_extender_1_out), .in1(bit_extender_2_out), .out(Dout), .sel(ExtSign));

  // Notes on the sheet:
  //   Dout: pull=down
  //   Din: pull=down
  //   ExtSign: pull=down
endmodule

module NoBrchIFU (
  input  CLK,
  input  Reset,
  output [31:0] Instr
);

  wire [29:0] adder_1_out, multiplexer_1_out, PC_q;

  Multiplexer #(.width(30), .disabled(0), .enable("false")) multiplexer_1 (
    .in0(adder_1_out), .in1(30'h3000), .out(multiplexer_1_out), .sel(Reset));
  Register #(.width(30)) PC (.D(multiplexer_1_out), .Q(PC_q), .clk(CLK));  // open: en, clr
  // Probe on PC_q
  // Probe on PC_q[4:0]
  Adder #(.width(30)) adder_1 (.a(PC_q), .b(30'h1), .out(adder_1_out));  // open: cin, cout
  ROM #(.addrWidth(5), .dataWidth(32)) rom_1 (.addr(PC_q[4:0]), .data(Instr));  // open: sel
  // Probe on Instr

  // Notes on the sheet:
  //   contents of rom_1 (hex, n*v repeats v):
  //   3c08000c 3c090022 12a8821 3c0a0038 3c0b004e 16a9023 3c0c1234 358d0087 36530065 272a023 291a821
  //   36b60043 ac160008 ac150004 8c170004 8c180008 2f8c821 336d023 34040010 34050018 ac99fffc acbafff8
  //   8c86fff8 8ca7fff4 34a20999 34c30888 ac820004 aca30000
endmodule

module Instr_TO_Ctl (
  input  addu,
  input  subu,
  input  ori,
  input  lui,
  input  lw,
  input  sw,
  input  beq,
  output RegDst,
  output ALUSrc,
  output MemToReg,
  output RegWrite,
  output MemWrite,
  output nPC_sel,
  output ExtOp,
  output ShiftSel,
  output ALUctr_add,
  output ALUctr_sub,
  output ALUctr_or
);

  or u_RegDst (RegDst, addu, subu);
  buf buffer_1 (MemToReg, lw);
  or u_ALUSrc (ALUSrc, ori, lw, sw);
  or u_RegWrite (RegWrite, addu, subu, lui, ori, lw);
  buf buffer_2 (MemWrite, sw);
  buf buffer_3 (nPC_sel, beq);
  or u_ExtOp (ExtOp, lw, sw, beq);
  buf buffer_4 (ShiftSel, lui);
  or ALUctr_2 (ALUctr_add, addu, lw, sw);
  buf buffer_5 (ALUctr_sub, subu);
  buf buffer_6 (ALUctr_or, ori);

  // Notes on the sheet:
  //   lui: pull=down
  //   MemWrite: pull=down
  //   subu: pull=down
  //   ori: pull=down
  //   ALUctr_sub: pull=down
  //   ALUctr_add: pull=down
  //   ALUctr_or: pull=down
  //   ShiftSel: pull=down
  //   addu: pull=down
  //   MemToReg: pull=down
  //   ALUSrc: pull=down
  //   sw: pull=down
  //   RegDst: pull=down
  //   nPC_sel: pull=down
  //   beq: pull=down
  //   ExtOp: pull=down
  //   RegWrite: pull=down
  //   lw: pull=down
endmodule

module Controller (
  input  [5:0] func,
  input  [5:0] op,
  output RegDst,
  output ALUSrc,
  output MemToReg,
  output RegWrite,
  output MemWrite,
  output nPC_sel,
  output ExtOp,
  output ShiftSel,
  output [2:0] ALUCtl
);

  wire op_func_to_instr_1_addu, op_func_to_instr_1_beq, op_func_to_instr_1_lui, op_func_to_instr_1_lw,
       op_func_to_instr_1_ori, op_func_to_instr_1_subu, op_func_to_instr_1_sw;

  Op_func_TO_Instr op_func_to_instr_1 (
    .addu(op_func_to_instr_1_addu), .subu(op_func_to_instr_1_subu), .ori(op_func_to_instr_1_ori),
    .lui(op_func_to_instr_1_lui), .lw(op_func_to_instr_1_lw), .sw(op_func_to_instr_1_sw),
    .beq(op_func_to_instr_1_beq), .op31(op[5]), .op30(op[4]), .op29(op[3]), .op28(op[2]), .op27(op[1]),
    .op26(op[0]), .fun5(func[5]), .fun4(func[4]), .fun3(func[3]), .fun2(func[2]), .fun1(func[1]),
    .fun0(func[0]));
  Instr_TO_Ctl instr_to_ctl_1 (
    .addu(op_func_to_instr_1_addu), .subu(op_func_to_instr_1_subu), .ori(op_func_to_instr_1_ori),
    .lw(op_func_to_instr_1_lw), .sw(op_func_to_instr_1_sw), .beq(op_func_to_instr_1_beq), .RegDst(RegDst),
    .ALUSrc(ALUSrc), .MemToReg(MemToReg), .RegWrite(RegWrite), .MemWrite(MemWrite), .nPC_sel(nPC_sel),
    .ExtOp(ExtOp), .ALUctr_add(ALUCtl[2]), .ALUctr_sub(ALUCtl[1]), .lui(op_func_to_instr_1_lui),
    .ShiftSel(ShiftSel), .ALUctr_or(ALUCtl[0]));

  // Notes on the sheet:
  //   ExtOp: pull=down
  //   ALUCtl: pull=down
  //   ShiftSel: pull=down
  //   RegDst: pull=down
  //   MemWrite: pull=down
  //   MemToReg: pull=down
  //   nPC_sel: pull=down
  //   RegWrite: pull=down
  //   ALUSrc: pull=down
endmodule

module InstrSplitter (
  input  [31:0] Instru,
  output [5:0] OpCode,
  output [5:0] func,
  output [4:0] _25_21,
  output [4:0] _20_16,
  output [4:0] _15_11,
  output [15:0] Imm
);


  assign _15_11 = Instru[15:11];
  assign _20_16 = Instru[20:16];
  assign _25_21 = Instru[25:21];
  assign func = Instru[5:0];
  assign Imm = Instru[15:0];
  assign OpCode = Instru[31:26];

  // Notes on the sheet:
  //   Imm: pull=down
  //   OpCode: pull=down
  //   Instru: pull=down
  //   _25_21: pull=down
  //   func: pull=down
  //   _20_16: pull=down
  //   _15_11: pull=down
endmodule

module Lshifter (
  input  [31:0] Din,
  input  [4:0] ShiftCnt,
  output [31:0] Dout
);

  Shifter #(.width(32)) shifter_1 (.in(Din), .\dist (ShiftCnt), .out(Dout));

  // Notes on the sheet:
  //   ShiftCnt: pull=down
  //   Dout: pull=down
  //   Din: pull=down
endmodule

module R_Cycle_Deprecated (
  input  in_1
);

  wire CLK, controller_1_regwrite;
  wire [2:0] controller_1_shiftsel;
  wire [4:0] instrsplitter_1__15_11, instrsplitter_1__20_16, instrsplitter_1__25_21;
  wire [5:0] instrsplitter_1_func, instrsplitter_1_opcode;
  wire [31:0] alu_1_aluout, grf_1_rd1, grf_1_rd2, nobrchifu_1_instr;

  Clock clock_1 (.out(CLK));
  NoBrchIFU nobrchifu_1 (.Instr(nobrchifu_1_instr), .CLK(CLK), .Reset(in_1));
  // Probe on nobrchifu_1_instr
  InstrSplitter instrsplitter_1 (
    .Instru(nobrchifu_1_instr), .OpCode(instrsplitter_1_opcode), .func(instrsplitter_1_func),
    ._25_21(instrsplitter_1__25_21), ._20_16(instrsplitter_1__20_16), ._15_11(instrsplitter_1__15_11));  // open: Imm
  // Probe on instrsplitter_1__20_16
  // Probe on instrsplitter_1__25_21
  // Probe on instrsplitter_1__15_11
  // Probe on alu_1_aluout
  Controller controller_1 (
    .func(instrsplitter_1_func), .op(instrsplitter_1_opcode), .RegWrite(controller_1_regwrite),
    .ShiftSel(controller_1_shiftsel[0]));  // open: RegDst, ALUSrc, MemToReg, MemWrite, nPC_sel, ExtOp, ALUCtl
  GRF grf_1 (
    .RD1_num(instrsplitter_1__25_21), .RD2_num(instrsplitter_1__20_16), .in_6(in_1),
    .W_num(instrsplitter_1__15_11), .WD(alu_1_aluout), .RD1(grf_1_rd1), .RD2(grf_1_rd2),
    .WE(controller_1_regwrite), .in_5(CLK));
  // Probe on grf_1_rd1
  ALU alu_1 (
    .ALUCtl(controller_1_shiftsel), .ALUOut(alu_1_aluout), .operand1(grf_1_rd1), .operand2(grf_1_rd2));  // open: Equal
  // Probe on grf_1_rd2
  // Probe on controller_1_shiftsel
  // Pins of 1 and 3 bits meet at controller_1_shiftsel

  // Other names for the same wires on the sheet: Reset = in_1
endmodule

module R_LS_Cycle_Deprecated (
  input  in_1
);

  wire ALUSrc, CLK, ExtOp, MemToReg, MemWrite, nPC_sel, RegDst, RegWrite;
  wire [2:0] ALUCtl;
  wire [4:0] instrsplitter_1__15_11, instrsplitter_1__20_16, instrsplitter_1__25_21, multiplexer_1_out;
  wire [5:0] instrsplitter_1_func, instrsplitter_1_opcode;
  wire [15:0] instrsplitter_1_imm;
  wire [31:0] alu_1_aluout, dm_1_rddata, ext_1_dout, grf_1_rd1, grf_1_rd2, multiplexer_2_out,
       multiplexer_3_out, nobrchifu_1_instr;

  Clock clock_1 (.out(CLK));
  NoBrchIFU nobrchifu_1 (.Instr(nobrchifu_1_instr), .CLK(CLK), .Reset(in_1));
  // Probe on nobrchifu_1_instr
  InstrSplitter instrsplitter_1 (
    .Instru(nobrchifu_1_instr), .OpCode(instrsplitter_1_opcode), .func(instrsplitter_1_func),
    ._25_21(instrsplitter_1__25_21), ._20_16(instrsplitter_1__20_16), ._15_11(instrsplitter_1__15_11),
    .Imm(instrsplitter_1_imm));
  // Probe on instrsplitter_1__25_21
  // Probe on instrsplitter_1__20_16
  // Probe on instrsplitter_1__15_11
  Controller controller_1 (
    .func(instrsplitter_1_func), .op(instrsplitter_1_opcode), .RegDst(RegDst), .ALUSrc(ALUSrc),
    .MemToReg(MemToReg), .RegWrite(RegWrite), .MemWrite(MemWrite), .nPC_sel(nPC_sel), .ExtOp(ExtOp),
    .ShiftSel(ALUCtl[0]));  // open: ALUCtl
  Multiplexer #(.width(5), .enable("false")) multiplexer_1 (
    .in0(instrsplitter_1__20_16), .in1(instrsplitter_1__15_11), .out(multiplexer_1_out), .sel(RegDst));
  EXT ext_1 (.Din(instrsplitter_1_imm), .Dout(ext_1_dout), .ExtSign(ExtOp));
  // Probe on multiplexer_3_out
  GRF grf_1 (
    .RD1_num(instrsplitter_1__25_21), .RD2_num(instrsplitter_1__20_16), .in_6(in_1),
    .W_num(multiplexer_1_out), .WD(multiplexer_3_out), .RD1(grf_1_rd1), .RD2(grf_1_rd2), .WE(RegWrite),
    .in_5(CLK));
  // Probe on grf_1_rd1
  ALU alu_1 (
    .ALUCtl(ALUCtl), .ALUOut(alu_1_aluout), .operand1(grf_1_rd1), .operand2(multiplexer_2_out));  // open: Equal
  Multiplexer #(.width(32), .enable("false")) multiplexer_2 (
    .in0(grf_1_rd2), .in1(ext_1_dout), .out(multiplexer_2_out), .sel(ALUSrc));
  // Probe on grf_1_rd2
  // Probe on ALUCtl
  Multiplexer #(.width(32), .enable("false")) multiplexer_3 (
    .in0(alu_1_aluout), .in1(dm_1_rddata), .out(multiplexer_3_out), .sel(MemToReg));
  // Probe on multiplexer_2_out
  DM dm_1 (
    .MemAddr(alu_1_aluout), .MemData(grf_1_rd2), .MemWrite(MemWrite), .RdData(dm_1_rddata), .CLK(CLK),
    .Reset(in_1));
  // Pins of 1 and 3 bits meet at ALUCtl

  // Other names for the same wires on the sheet: Reset = in_1
endmodule

module NoBrchCycle (
  input  in_1
);

  wire ALUSrc, CLK, ExtOp, MemToReg, MemWrite, nPC_sel, RegDst, RegWrite, ShiftSel;
  wire [2:0] ALUCtl;
  wire [4:0] instrsplitter_1__15_11, instrsplitter_1__20_16, instrsplitter_1__25_21, multiplexer_1_out;
  wire [5:0] instrsplitter_1_func, instrsplitter_1_opcode;
  wire [15:0] instrsplitter_1_imm;
  wire [31:0] alu_1_aluout, dm_1_rddata, ext_1_dout, grf_1_rd1, grf_1_rd2, lshifter_1_dout,
       multiplexer_2_out, multiplexer_3_out, multiplexer_4_out, multiplexer_5_out, nobrchifu_1_instr;

  Clock clock_1 (.out(CLK));
  NoBrchIFU nobrchifu_1 (.Instr(nobrchifu_1_instr), .CLK(CLK), .Reset(in_1));
  // Probe on nobrchifu_1_instr
  InstrSplitter instrsplitter_1 (
    .Instru(nobrchifu_1_instr), .OpCode(instrsplitter_1_opcode), .func(instrsplitter_1_func),
    ._25_21(instrsplitter_1__25_21), ._20_16(instrsplitter_1__20_16), ._15_11(instrsplitter_1__15_11),
    .Imm(instrsplitter_1_imm));
  // Probe on instrsplitter_1__25_21
  // Probe on instrsplitter_1__20_16
  // Probe on instrsplitter_1__15_11
  Controller controller_1 (
    .func(instrsplitter_1_func), .op(instrsplitter_1_opcode), .RegDst(RegDst), .ALUSrc(ALUSrc),
    .MemToReg(MemToReg), .RegWrite(RegWrite), .MemWrite(MemWrite), .nPC_sel(nPC_sel), .ExtOp(ExtOp),
    .ALUCtl(ALUCtl), .ShiftSel(ShiftSel));
  Multiplexer #(.width(5), .enable("false")) multiplexer_1 (
    .in0(instrsplitter_1__20_16), .in1(instrsplitter_1__15_11), .out(multiplexer_1_out), .sel(RegDst));
  EXT ext_1 (.Din(instrsplitter_1_imm), .Dout(ext_1_dout), .ExtSign(ExtOp));
  // Probe on ext_1_dout
  Lshifter lshifter_1 (.Din(ext_1_dout), .ShiftCnt(5'b10000), .Dout(lshifter_1_dout));
  // Probe on lshifter_1_dout
  // Probe on multiplexer_2_out
  GRF grf_1 (
    .RD1_num(instrsplitter_1__25_21), .RD2_num(instrsplitter_1__20_16), .in_6(in_1),
    .W_num(multiplexer_1_out), .WD(multiplexer_2_out), .RD1(grf_1_rd1), .RD2(grf_1_rd2), .WE(RegWrite),
    .in_5(CLK));
  Multiplexer #(.width(32), .enable("false")) multiplexer_2 (
    .in0(multiplexer_5_out), .in1(multiplexer_3_out), .out(multiplexer_2_out), .sel(ShiftSel));
  Multiplexer #(.width(32), .enable("false")) multiplexer_3 (
    .in0(ext_1_dout), .in1(lshifter_1_dout), .out(multiplexer_3_out), .sel(ShiftSel));
  // Probe on grf_1_rd1
  // Probe on multiplexer_3_out
  // Probe on grf_1_rd2
  ALU alu_1 (
    .ALUCtl(ALUCtl), .ALUOut(alu_1_aluout), .operand1(grf_1_rd1), .operand2(multiplexer_4_out));  // open: Equal
  Multiplexer #(.width(32), .enable("false")) multiplexer_4 (
    .in0(grf_1_rd2), .in1(multiplexer_3_out), .out(multiplexer_4_out), .sel(ALUSrc));
  // Probe on ALUCtl
  Multiplexer #(.width(32), .enable("false")) multiplexer_5 (
    .in0(alu_1_aluout), .in1(dm_1_rddata), .out(multiplexer_5_out), .sel(MemToReg));
  // Probe on multiplexer_4_out
  // Probe on alu_1_aluout
  DM dm_1 (
    .MemAddr(alu_1_aluout), .MemData(grf_1_rd2), .MemWrite(MemWrite), .RdData(dm_1_rddata), .CLK(CLK),
    .Reset(in_1));

  // Other names for the same wires on the sheet: Reset = in_1
endmodule
